# Fritzing sketch mood lamp (saved by Fritzing 0.9.6b)

parts:
  U1 = WS2812 RGB LED strip
  DHT1 = Humidity and Temperature Sensor DHT11
  WeMos_D1_Mini1 = WeMos D1 Mini

nets:
  N1: U1.GND, DHT1.GND_1, WeMos_D1_Mini1.G
  VCC: U1.VCC, WeMos_D1_Mini1.5V
  N2: U1.DIN, WeMos_D1_Mini1.D4
  VCC_2: DHT1.Vcc, WeMos_D1_Mini1.3V3
  N3: DHT1.Data-signal, WeMos_D1_Mini1.D5

custom parts:
  WS2812 RGB LED strip: WS2812 strip
  Humidity and Temperature Sensor DHT11: Digital relative humidity & temperature sensor DHT11
